# Fritzing sketch Wiring-Lengkap (saved by Fritzing 0.9.5d)
breadboards: 2

parts:
  CPU1 = NodeMCU WROOM ESP 32
  U1 = DFRobot SEN0189 [package=THT]
  S1 = PH meter [package=THT]
  M1 = ph-4502c [package=THT]  # not connected
  A1 = tds-sensor-meter-v1.0_1
  U2 = Turbidity Sensor Probe [package=THT]
  CPU2 = NodeMCU WROOM ESP 32
  U3 = DFRobot SEN0189 [package=THT]
  S2 = PH meter [package=THT]
  A2 = tds-sensor-meter-v1.0_1  # not connected
  U4 = Turbidity Sensor Probe [package=THT]

nets:
  N1: CPU1.pin_5, S1.pin1
  N2: CPU1.pin_6, A1.pin1
  N3: CPU1.pin_7, U1.P1_1
  N4: CPU1.pin_17, S1.pin2, A1.pin2
  N5: CPU1.pin_18, U1.P1_3, A1.pin3
  N6: U1.P2_1, U2.pin1
  N7: U1.P2_2, U2.VCC
  N8: U1.P2_3, U2.pin2
  N9: CPU2.pin_6, S2.pin1
  N10: U3.P2_1, U4.pin1
  N11: U3.P2_2, U4.VCC
  N12: U3.P2_3, U4.pin2

custom parts:
  NodeMCU WROOM ESP 32: 30 pol Development Kit
  DFRobot SEN0189: Turbidity sensor of DFRobot SEN0189
  ph-4502c: ph-4502c PH Meter.
  : TDS Meter V1.0 Development Board Water Meter Filter Measuring Water Sensor Module.
  Turbidity Sensor Probe: Turbidity sensor probe to the DFRobot measure module.
